// Logisim project microprocessor.circ as structural Verilog: 4 circuits, main circuit CPU
module CPU (
);

  wire Clk, Decode, Execute, Fetch, I_Type, J_Type, P_Type, R_Type;
  wire [2:0] ALU_SEL;
  wire [7:0] Value_Given;
  wire [12:0] inst;

  Control_Unit Control_Unit (
    .I_Type(I_Type), .R_Type(R_Type), .P_Type(P_Type), .J_Type(J_Type), .Fetch(Fetch), .Decode(Decode),
    .Execute(Execute), .Instruction(inst), .Clk(Clk), .ALU_SEL(ALU_SEL), .Value_Given(Value_Given));
endmodule

// ALU
module AritmaticLogicUnit (
  input  [7:0] Input1,
  input  [7:0] Input2,
  input  [2:0] ALU_Sel,
  input  carryoutadd,
  input  carryoutsub,
  output [7:0] Output
);

  wire [7:0] adda, anda, ora, shiftL, shiftR, suba;

  Adder adder_1 (.a(Input1), .b(Input2), .out(adda), .cin(1'b0), .cout(carryoutadd));
  Subtractor subtractor_1 (.a(Input1), .b(Input2), .out(suba), .bin(1'b0), .bout(carryoutsub));
  assign anda = Input1 & Input2;  // AND_Gate anda, 8 bits wide
  assign ora = Input1 | Input2;  // OR_Gate ora, 8 bits wide
  Shifter shifter_1 (.in(Input1), .\dist (3'b001), .out(shiftL));
  Shifter #(.shift("lr")) shifter_2 (.in(Input1), .\dist (3'b001), .out(shiftR));
  Multiplexer #(.select(3), .width(8), .enable("false")) multiplexer_1 (
    .in0(adda), .in1(suba), .in2(anda), .in3(ora), .in4(Input1), .in5(shiftL), .in6(shiftR), .in7({8{1'b0}}),
    .out(Output), .sel(ALU_Sel));

  // Other names for the same wires on the sheet: mova[7:0] = Input1
endmodule

module Accumulator (
  input  [7:0] Input,
  input  Clock,
  input  Exec,
  input  AscSet0,
  output [7:0] \output 
);

  Pull_Resistor pull_resistor_1 (.node(AscSet0));
  D_Flip_Flop d_ff_1 (.clk(Clock), .D(Input[7]), .Q(\output [7]), .en(Exec), .reset(AscSet0));  // open: Qn, preset
  D_Flip_Flop d_ff_2 (.clk(Clock), .D(Input[6]), .Q(\output [6]), .en(Exec), .reset(AscSet0));  // open: Qn, preset
  D_Flip_Flop d_ff_3 (.clk(Clock), .D(Input[5]), .Q(\output [5]), .en(Exec), .reset(AscSet0));  // open: Qn, preset
  D_Flip_Flop d_ff_4 (.clk(Clock), .D(Input[4]), .Q(\output [4]), .en(Exec), .reset(AscSet0));  // open: Qn, preset
  D_Flip_Flop d_ff_5 (.clk(Clock), .D(Input[3]), .Q(\output [3]), .en(Exec), .reset(AscSet0));  // open: Qn, preset
  D_Flip_Flop d_ff_6 (.clk(Clock), .D(Input[2]), .Q(\output [2]), .en(Exec), .reset(AscSet0));  // open: Qn, preset
  D_Flip_Flop d_ff_7 (.clk(Clock), .D(Input[1]), .Q(\output [1]), .en(Exec), .reset(AscSet0));  // open: Qn, preset
  D_Flip_Flop d_ff_8 (.clk(Clock), .D(Input[0]), .Q(\output [0]), .en(Exec), .reset(AscSet0));  // open: Qn, preset

  // Other names for the same wires on the sheet: in0 = Input[0]; in1 = Input[1]; in2 = Input[2]; in3 = Input[3];
  //   in4 = Input[4]; in5 = Input[5]; in6 = Input[6]; in7 = Input[7]; out0 = \output [0]; out1 = \output [1];
  //   out2 = \output [2]; out3 = \output [3]; out4 = \output [4]; out5 = \output [5]; out6 = \output [6];
  //   out7 = \output [7]
endmodule

module Control_Unit (
  input  [12:0] Instruction,
  input  Clk,
  output I_Type,
  output R_Type,
  output P_Type,
  output J_Type,
  output Fetch,
  output Decode,
  output Execute,
  output [7:0] Value_Given,
  output [2:0] ALU_SEL
);

  wire Fetch_2_out, not_1_out, not_2_out, not_3_out, not_4_out, not_5_out, not_6_out, not_7_out, not_8_out,
       not_9_out;
  wire [2:0] register_1_q;
  wire [2:2] or_1_out;

  Decoder #(.select(2), .enable("false")) decoder_1 (
    .out0(I_Type), .out1(R_Type), .out2(P_Type), .out3(J_Type), .sel(Instruction[12:11]));
  Register #(.width(3)) register_1 (
    .D({or_1_out[2], Decode, Execute}), .en(1'b1), .Q(register_1_q), .clk(Clk));  // open: clr
  not not_1 (not_1_out, register_1_q[0]);
  not not_2 (not_2_out, register_1_q[2]);
  and u_Execute (Execute, not_1_out, register_1_q[1], not_2_out);
  not not_3 (not_3_out, register_1_q[0]);
  not not_4 (not_4_out, register_1_q[1]);
  and u_Decode (Decode, not_3_out, not_4_out, register_1_q[2]);
  or or_1 (or_1_out[2], Fetch, Fetch_2_out);
  not not_5 (not_5_out, register_1_q[1]);
  not not_6 (not_6_out, register_1_q[2]);
  and u_Fetch (Fetch, register_1_q[0], not_5_out, not_6_out);
  not not_7 (not_7_out, register_1_q[1]);
  not not_8 (not_8_out, register_1_q[2]);
  not not_9 (not_9_out, register_1_q[0]);
  and Fetch_2 (Fetch_2_out, not_9_out, not_7_out, not_8_out);

  assign ALU_SEL = Instruction[10:8];
  assign Value_Given = Instruction[7:0];

  // Notes on the sheet:
  //   Fetch
  //   Decode
  //   Execute
endmodule
